# Fritzing sketch buratino (saved by Fritzing 0.9.3b)
breadboards: 1
perfboards: 2

parts:
  R1 = Resistor [tolerance=±5% resistance=220 package=THT]  # not connected
  S1 = Pushbutton [package="[THT]"]
  Q1 = NPN-Transistor [package="TO92 [THT]"]  # not connected
  R2 = Resistor [tolerance=±5% resistance=220 package=THT]

nets:
  N1: S1.Pin_1, S1.Pin_2, R2.Pin_0
  N2: S1.Pin_3, S1.Pin_4
